# Fritzing sketch wg-brew-plus-1.0 (saved by Fritzing 0.9.3b)
circuit board: 9.8cm x 6.3cm
breadboards: 1

parts:
  BT2_BT3 = screw terminal, 2 pins
  BT6_BT7 = screw terminal, 2 pins
  5V_BT1 = screw terminal, 2 pins
  D08_D09 = screw terminal, 2 pins
  3V3_D13 = screw terminal, 2 pins
  A1_GND = screw terminal, 2 pins
  A3_A2 = screw terminal, 2 pins
  A5_A4 = screw terminal, 2 pins
  GND_5V = screw terminal, 2 pins
  -_VIN_+ = screw terminal, 2 pins
  BT-RESET = screw terminal, 2 pins
  D-BT3 = Rectifier Diode [part_number=1N4001 package="300 mil [THT]"]
  D-BT4 = Rectifier Diode [part_number=1N4001 package="300 mil [THT]"]
  D-BT5 = Rectifier Diode [part_number=1N4001 package="300 mil [THT]"]
  D-BT6 = Rectifier Diode [part_number=1N4001 package="300 mil [THT]"]
  D-BT7 = Rectifier Diode [part_number=1N4001 package="300 mil [THT]"]
  D-BT2 = Rectifier Diode [part_number=1N4001 package="300 mil [THT]"]
  D10_D12 = screw terminal, 2 pins
  BT4_BT5 = screw terminal, 2 pins
  BUZZER = Buzzer 12mm [package=buzzer-12mm-ns-kit]
  ARDUINO-NANO = Arduino Nano (Rev3.0)
  R-PD-A0 = Resistor [tolerance=±5% resistance=220 package=THT]
  R-PU-A4 = Resistor [tolerance=±5% resistance=220 package=THT]
  R-PU-A5 = Resistor [tolerance=±5% resistance=220 package=THT]
  R-PD-A2 = Resistor [tolerance=±5% resistance=220 package=THT]
  R-PD-A3 = Resistor [tolerance=±5% resistance=220 package=THT]
  R-PD-A1 = Resistor [tolerance=±5% resistance=220 package=THT]
  DISPLAY_16X2 = LCD-16X2 [package=lcd-16x2_noholes]

nets:
  N1: BT2_BT3.pin1, D-BT3.anode, D-BT4.cathode
  N2: BT2_BT3.pin2, D-BT3.cathode, D-BT2.anode
  N3: BT6_BT7.pin1, D-BT7.anode
  N4: BT6_BT7.pin2, D-BT6.anode, D-BT7.cathode
  N5: 5V_BT1.pin1, D-BT2.cathode, ARDUINO-NANO.A0, R-PD-A0.Pin_0
  5V: 5V_BT1.pin2, GND_5V.pin1, ARDUINO-NANO.5V, R-PU-A4.Pin_1, R-PU-A5.Pin_1, DISPLAY_16X2.VDD, DISPLAY_16X2.A
  N6: D08_D09.pin1, ARDUINO-NANO.D8
  N7: D08_D09.pin2, ARDUINO-NANO.D9
  N8: 3V3_D13.pin1, ARDUINO-NANO.3V3
  N9: 3V3_D13.pin2, ARDUINO-NANO.D13/SCK
  N10: A1_GND.pin1, ARDUINO-NANO.A1, R-PD-A1.Pin_0
  GND: A1_GND.pin2, GND_5V.pin2, -_VIN_+.pin2, BT-RESET.pin2, BUZZER.2, ARDUINO-NANO.GND, R-PD-A0.Pin_1, R-PD-A2.Pin_1, R-PD-A3.Pin_1, R-PD-A1.Pin_1, DISPLAY_16X2.VSS, DISPLAY_16X2.VO, DISPLAY_16X2.R_W, DISPLAY_16X2.K
  N11: A3_A2.pin1, ARDUINO-NANO.A3, R-PD-A3.Pin_0
  N12: A3_A2.pin2, ARDUINO-NANO.A2, R-PD-A2.Pin_0
  N13: A5_A4.pin1, ARDUINO-NANO.A5, R-PU-A5.Pin_0
  N14: A5_A4.pin2, ARDUINO-NANO.A4, R-PU-A4.Pin_0
  N15: -_VIN_+.pin1, ARDUINO-NANO.VIN
  N16: BT-RESET.pin1, ARDUINO-NANO.RESET
  N17: D-BT4.anode, D-BT5.cathode, BT4_BT5.pin2
  N18: D-BT5.anode, D-BT6.cathode, BT4_BT5.pin1
  N19: D10_D12.pin1, ARDUINO-NANO.D10
  N20: D10_D12.pin2, ARDUINO-NANO.D12/MISO
  N21: BUZZER.1, ARDUINO-NANO.D11/MOSI
  N22: ARDUINO-NANO.D2, DISPLAY_16X2.RS
  N23: ARDUINO-NANO.D3, DISPLAY_16X2.E
  N24: ARDUINO-NANO.D4, DISPLAY_16X2.DB4
  N25: ARDUINO-NANO.D5, DISPLAY_16X2.DB5
  N26: ARDUINO-NANO.D6, DISPLAY_16X2.DB6
  N27: ARDUINO-NANO.D7, DISPLAY_16X2.DB7

notes:
  WG - BREW PLUS v1.0
  WG-BREW PLUS V1.0
